// Logisim project cpu.circ as structural Verilog: 4 circuits, main circuit main
module main (
);

  wire alu_1_p4, Clk, clock_1_out, control_1_disp, control_1_dmwe, control_1_halt, control_1_pcaddsrc,
       control_1_pcen, control_1_rfr1src, control_1_rfwe;
  wire [1:0] control_1_aluysrc, control_1_pcsrc, control_1_rfdinsrc, control_1_rfrwsrc;
  wire [3:0] control_1_aluop, Disp_q, Disp_q_2, Disp_q_3, Disp_q_4, Disp_q_5, Disp_q_6, Disp_q_7, Disp_q_8;
  wire [4:0] insanalyse_1_rd, insanalyse_1_rs, insanalyse_1_rt, insanalyse_1_shamt, multiplexer_2_out,
       multiplexer_3_out;
  wire [5:0] insanalyse_1_funct, insanalyse_1_op;
  wire [9:0] alu_1_p5;
  wire [15:0] insanalyse_1_immediate16;
  wire [25:0] insanalyse_1_immediate26;
  wire [31:0] adder_1_out, adder_2_out, bit_extender_1_out, bit_extender_2_out, bit_extender_3_out,
       bit_extender_4_out, counter_1_q, main_1_a0_value, main_1_reg1, main_1_reg2_2, main_1_v0_value,
       multiplexer_1_out, multiplexer_4_out, multiplexer_5_out, multiplexer_6_out, PC_q, ram_1_data,
       rom_1_data;
  wire [31:10] alu_1_p5_2;

  assign bit_extender_1_out = {{6{1'b0}}, insanalyse_1_immediate26};  // Bit_Extender bit_extender_1
  Multiplexer #(.select(2), .width(32), .enable("false")) multiplexer_1 (
    .in0(main_1_reg1), .in1(adder_1_out), .in2(adder_2_out), .in3(bit_extender_1_out),
    .out(multiplexer_1_out), .sel(control_1_pcsrc));
  Register #(.width(32)) PC (.D(multiplexer_1_out), .en(control_1_pcen), .Q(PC_q), .clk(Clk), .clr(1'b0));
  Adder #(.width(32)) adder_1 (.a(32'h1), .b(PC_q), .out(adder_1_out), .cin(1'b0));  // open: cout
  Hex_Digit_Display hex_digit_display_1 (.value(Disp_q_7), .dp(1'b0));
  Hex_Digit_Display hex_digit_display_2 (.value(Disp_q_8), .dp(1'b0));
  Hex_Digit_Display hex_digit_display_3 (.value(Disp_q_5), .dp(1'b0));
  Hex_Digit_Display hex_digit_display_4 (.value(Disp_q_6), .dp(1'b0));
  Hex_Digit_Display hex_digit_display_5 (.value(Disp_q_4), .dp(1'b0));
  Hex_Digit_Display hex_digit_display_6 (.value(Disp_q_3), .dp(1'b0));
  Hex_Digit_Display hex_digit_display_7 (.value(Disp_q), .dp(1'b0));
  Hex_Digit_Display hex_digit_display_8 (.value(Disp_q_2), .dp(1'b0));
  ROM #(.addrWidth(10), .dataWidth(32)) rom_1 (.addr(PC_q[9:0]), .data(rom_1_data), .sel(1'b1));
  // Probe on counter_1_q
  Counter #(.width(32), .max('hffffffff)) counter_1 (.Q(counter_1_q), .clk(Clk));  // open: load, D, count, carry, clr
  Clock clock_1 (.out(clock_1_out));
  and and_1 (Clk, clock_1_out, ~control_1_halt);  // AND_Gate
  Register #(.width(32), .trigger("high")) Disp (
    .D(main_1_a0_value), .en(1'b1),
    .Q({Disp_q_8, Disp_q_7, Disp_q_6, Disp_q_5, Disp_q_4, Disp_q_3, Disp_q_2, Disp_q}), .clk(control_1_disp),
    .clr(1'b0));
  InsAnalyse insanalyse_1 (
    .Ins(rom_1_data), .OP(insanalyse_1_op), .Rs(insanalyse_1_rs), .Rt(insanalyse_1_rt), .Rd(insanalyse_1_rd),
    .Shamt(insanalyse_1_shamt), .funct(insanalyse_1_funct), .Immediate16(insanalyse_1_immediate16),
    .Immediate26(insanalyse_1_immediate26));
  Control control_1 (
    .Equal(alu_1_p4), .v0(main_1_v0_value), .OP(insanalyse_1_op), .funct(insanalyse_1_funct),
    .PCSrc(control_1_pcsrc), .PCAddSrc(control_1_pcaddsrc), .PCEn(control_1_pcen),
    .RFR1Src(control_1_rfr1src), .RFRWSrc(control_1_rfrwsrc), .RFDinSrc(control_1_rfdinsrc),
    .RFWE(control_1_rfwe), .ALUYSrc(control_1_aluysrc), .ALUOP(control_1_aluop), .DMWE(control_1_dmwe),
    .Halt(control_1_halt), .Disp(control_1_disp));
  Multiplexer #(.width(5), .enable("false")) multiplexer_2 (
    .in0(insanalyse_1_rs), .in1(insanalyse_1_rt), .out(multiplexer_2_out), .sel(control_1_rfr1src));
  Multiplexer #(.select(2), .width(5), .enable("false")) multiplexer_3 (
    .in0(insanalyse_1_rt), .in1(insanalyse_1_rd), .in2({5{1'b1}}), .out(multiplexer_3_out),
    .sel(control_1_rfrwsrc));  // open: in3
  Multiplexer #(.select(2), .width(32), .enable("false")) multiplexer_4 (
    .in0(adder_2_out), .in1(ram_1_data), .in2({alu_1_p5_2, alu_1_p5}), .out(multiplexer_4_out),
    .sel(control_1_rfdinsrc));  // open: in3
  regfile_cpu_main main_1 (
    .Reg1_num(multiplexer_2_out), .Reg2(insanalyse_1_rt), .Write_Reg_num(multiplexer_3_out),
    .Din(multiplexer_4_out), .Write_Enable(control_1_rfwe), .Clock(Clk), .Reg1(main_1_reg1),
    .Reg2_2(main_1_reg2_2), .v0_Value(main_1_v0_value), .a0_Value(main_1_a0_value));  // open: s0_Value, s1_Value, s2_Value, ra_Value
  assign bit_extender_2_out = {{27{1'b0}}, insanalyse_1_shamt};  // Bit_Extender bit_extender_2
  assign bit_extender_3_out = {{16{insanalyse_1_immediate16[15]}}, insanalyse_1_immediate16};  // Bit_Extender bit_extender_3
  assign bit_extender_4_out = {{16{1'b0}}, insanalyse_1_immediate16};  // Bit_Extender bit_extender_4
  Multiplexer #(.select(2), .width(32), .enable("false")) multiplexer_5 (
    .in0(main_1_reg2_2), .in1(bit_extender_2_out), .in2(bit_extender_3_out), .in3(bit_extender_4_out),
    .out(multiplexer_5_out), .sel(control_1_aluysrc));
  // ALU alu_1: pin names not known; wires that end beside it: main_1_reg1, multiplexer_5_out, control_1_aluop, alu_1_p4, {alu_1_p5_2, alu_1_p5}
  Multiplexer #(.width(32), .enable("false")) multiplexer_6 (
    .in0({32{1'b0}}), .in1(bit_extender_3_out), .out(multiplexer_6_out), .sel(control_1_pcaddsrc));
  Adder #(.width(32)) adder_2 (.a(adder_1_out), .b(multiplexer_6_out), .out(adder_2_out), .cin(1'b0));  // open: cout
  RAM #(.addrWidth(10), .dataWidth(32), .bus("separate")) ram_1 (
    .addr(alu_1_p5), .din(main_1_reg2_2), .data(ram_1_data), .str(control_1_dmwe), .sel(1'b1), .clk(Clk),
    .ld(1'b1), .clr(1'b0));

  // Notes on the sheet:
  //   contents of rom_1 (hex, n*v repeats v):
  //   20110001 8000c05 20110001 20120002 20130003 8000c09 20110001 20120002 20130003 8000c0d 20110001
  //   20120002 20130003 8000c11 20110001 20120002 20130003 c000cb8 20100001 20110001 118fc0 112020
  //   20020022 c 118882 12200001 8000c15 112020 20020022 c 20110001 118880 112020 20020022 c 12200001
  //   8000c1f 20110001 118fc0 112020 20020022 c 1188c3 112020 20020022 c 118903 112020 20020022 c 118903
  //   112020 20020022 c 118903 112020 20020022 c 118903 112020 20020022 c 118903 112020 20020022 c 118903
  //   112020 20020022 c 118903 112020 20020022 c 20100001 109fc0 139fc3 8021 2012000c 24160003 26100001
  //   3210000f 20080008 20090001 139900 2709825 132020 20020022 c 1094022 1500fff9 22100001 2018000f
  //   2188024 108700 20080008 20090001 139902 2709825 132021 20020022 c 1094022 1500fff9 108702 2c9b022
  //   12c00001 8000c50 4020 1084027 84400 3508ffff 82021 20020022 c 2010ffff 20110000 ae300000 22100001
  //   22310004 ae300000 22100001 22310004 ae300000 22100001 22310004 ae300000 22100001 22310004 ae300000
  //   22100001 22310004 ae300000 22100001 22310004 ae300000 22100001 22310004 ae300000 22100001 22310004
  //   ae300000 22100001 22310004 ae300000 22100001 22310004 ae300000 22100001 22310004 ae300000 22100001
  //   22310004 ae300000 22100001 22310004 ae300000 22100001 22310004 ae300000 22100001 22310004 ae300000
  //   22100001 22310004 22100001 8020 2011003c 8e130000 8e340000 274402a 11000002 ae330000 ae140000
  //   2231fffc 1611fff8 102020 20020022 c 22100004 2011003c 1611fff2 2002000a c 20100000 22100001 102020
  //   20020022 c 22100002 102020 20020022 c 22100003 102020 20020022 c 22100004 102020 20020022 c 22100005
  //   102020 20020022 c 22100006 102020 20020022 c 22100007 102020 20020022 c 22100008 102020 20020022
  //   20020022 c 3e00008
endmodule

module InsAnalyse (
  input  [31:0] Ins,
  output [5:0] OP,
  output [4:0] Rs,
  output [4:0] Rt,
  output [4:0] Rd,
  output [4:0] Shamt,
  output [5:0] funct,
  output [15:0] Immediate16,
  output [25:0] Immediate26
);


  assign funct = Ins[5:0];
  assign Immediate16 = Ins[15:0];
  assign Immediate26 = Ins[25:0];
  assign OP = Ins[31:26];
  assign Rd = Ins[15:11];
  assign Rs = Ins[25:21];
  assign Rt = Ins[20:16];
  assign Shamt = Ins[10:6];
endmodule

module Control (
  input  Equal,
  input  [31:0] v0,
  input  [5:0] OP,
  input  [5:0] funct,
  output [1:0] PCSrc,
  output PCAddSrc,
  output PCEn,
  output RFR1Src,
  output [1:0] RFRWSrc,
  output [1:0] RFDinSrc,
  output RFWE,
  output [1:0] ALUYSrc,
  output [3:0] ALUOP,
  output DMWE,
  output Halt,
  output Disp
);

  wire add, addi, addiu, addu, \and , and_3_out, and_4_out, and_5_out, and_6_out, andi, beq, bne,
       decoder_1_out0, decoder_2_out0, decoder_2_out1, decoder_4_out0, decoder_4_out1, j, jr, \nor ,
       not_1_out, not_2_out, \or , ori, sll, slt, slti, sltu, sra, srl, sub, syscall, v0_10;
  wire [7:0] or_6_out;
  wire [31:0] subtractor_1_out;

  Decoder #(.select(5), .disabled(0)) decoder_1 (
    .out0(decoder_1_out0), .out2(j), .out3(RFRWSrc[1]), .out4(beq), .out5(bne), .out8(addi), .out9(addiu),
    .out10(slti), .out12(andi), .out13(ori), .sel(OP[4:0]), .en(decoder_2_out0));  // open: out1, out6, out7, out11, out14, out15, out16, out17, out18, out19, out20, out21, out22, out23, out24, out25, out26, out27, out28, out29, out30, out31
  Decoder #(.enable("false")) decoder_2 (.out0(decoder_2_out0), .out1(decoder_2_out1), .sel(OP[5]));
  Decoder #(.select(5), .disabled(0)) decoder_3 (
    .out3(RFDinSrc[0]), .out11(DMWE), .sel(OP[4:0]), .en(decoder_2_out1));  // open: out0, out1, out2, out4, out5, out6, out7, out8, out9, out10, out12, out13, out14, out15, out16, out17, out18, out19, out20, out21, out22, out23, out24, out25, out26, out27, out28, out29, out30, out31
  or or_1 (PCAddSrc, beq, bne);
  or or_2 (RFR1Src, sll, sra, srl);
  nor nor_1 (RFDinSrc[1], RFDinSrc[0], RFRWSrc[1]);
  and and_1 (Halt, syscall, v0_10);
  and and_2 (Disp, syscall, ~v0_10);  // AND_Gate
  Subtractor #(.width(32)) subtractor_1 (.a(v0), .b(32'ha), .out(subtractor_1_out));  // open: bin, bout
  not not_1 (not_1_out, Equal);
  and and_3 (and_3_out, beq, Equal);
  and and_4 (and_4_out, bne, not_2_out);
  not not_2 (not_2_out, Equal);
  nor nor_2 (RFWE, DMWE, beq, bne, j, jr, syscall);
  or or_3 (ALUYSrc[1], addi, addiu, andi, ori, RFDinSrc[0], DMWE, slti);
  or or_4 (ALUYSrc[0], andi, sll, sra, srl, ori);
  or or_5 (ALUOP[3], \or , ori, \nor , slt, slti, sltu);
  assign or_6_out = subtractor_1_out[7:0] | subtractor_1_out[15:8] | subtractor_1_out[23:16] | subtractor_1_out[31:24];  // OR_Gate or_6, 8 bits wide
  and and_5 (and_5_out, beq, Equal);
  and and_6 (and_6_out, bne, not_1_out);
  nor nor_3 (PCSrc[0], and_3_out, and_4_out, jr);
  or or_7 (RFRWSrc[0], add, addu, \and , sll, sra, srl, sub, \or , \nor , slt, sltu);
  or or_8 (ALUOP[2], add, addi, addiu, addu, \and , andi, sub, RFDinSrc[0], DMWE, beq, bne, sltu);
  or or_9 (ALUOP[1], \and , andi, srl, sub, \nor , beq, bne, slt, slti);
  or or_10 (ALUOP[0], add, addi, addiu, addu, \and , andi, sra, RFDinSrc[0], DMWE, slt, slti);
  or or_11 (PCSrc[1], and_5_out, and_6_out, j, RFRWSrc[1]);
  nor nor_4 (v0_10, or_6_out[0], or_6_out[1], or_6_out[2], or_6_out[3], or_6_out[4], or_6_out[5], or_6_out[6], or_6_out[7]);
  Decoder #(.disabled(0)) decoder_4 (.out0(decoder_4_out0), .out1(decoder_4_out1), .sel(funct[5]), .en(decoder_1_out0));
  Decoder #(.select(5), .disabled(0)) decoder_5 (
    .out0(sll), .out2(srl), .out3(sra), .out8(jr), .out12(syscall), .sel(funct[4:0]), .en(decoder_4_out0));  // open: out1, out4, out5, out6, out7, out9, out10, out11, out13, out14, out15, out16, out17, out18, out19, out20, out21, out22, out23, out24, out25, out26, out27, out28, out29, out30, out31
  Decoder #(.select(5), .disabled(0)) decoder_6 (
    .out0(add), .out1(addu), .out2(sub), .out4(\and ), .out5(\or ), .out7(\nor ), .out10(slt), .out11(sltu),
    .sel(funct[4:0]), .en(decoder_4_out1));  // open: out3, out6, out8, out9, out12, out13, out14, out15, out16, out17, out18, out19, out20, out21, out22, out23, out24, out25, out26, out27, out28, out29, out30, out31

  assign PCEn = 1'b1;

  // Other names for the same wires on the sheet: lw = RFDinSrc[0]; jal = RFRWSrc[1]; sw = DMWE
endmodule

module test (
);

  wire clock_1_out;
  wire [31:0] adder_1_out, PC_q, rom_1_data;

  Clock clock_1 (.out(clock_1_out));
  Register #(.width(32)) PC (.D(adder_1_out), .Q(PC_q), .clk(clock_1_out));  // open: en, clr
  Adder #(.width(32)) adder_1 (.a(32'h1), .b(PC_q), .out(adder_1_out));  // open: cin, cout
  ROM #(.addrWidth(10), .dataWidth(32)) rom_1 (.addr(PC_q[9:0]), .data(rom_1_data));  // open: sel

  // Notes on the sheet:
  //   contents of rom_1 (hex, n*v repeats v):
  //   20110001 8000c05 20110001 20120002 20130003 8000c09 20110001 20120002 20130003 8000c0d 20110001
  //   20120002 20130003 8000c11 20110001 20120002 20130003 c000cb8 20100001 20110001 118fc0 112020
  //   20020022 c 118882 12200001 8000c15 112020 20020022 c 20110001 118880 112020 20020022 c 12200001
  //   8000c1f 20110001 118fc0 112020 20020022 c 1188c3 112020 20020022 c 118903 112020 20020022 c 118903
  //   112020 20020022 c 118903 112020 20020022 c 118903 112020 20020022 c 118903 112020 20020022 c 118903
  //   112020 20020022 c 118903 112020 20020022 c 20100001 109fc0 139fc3 8021 2012000c 24160003 26100001
  //   3210000f 20080008 20090001 139900 2709825 132020 20020022 c 1094022 1500fff9 22100001 2018000f
  //   2188024 108700 20080008 20090001 139902 2709825 132021 20020022 c 1094022 1500fff9 108702 2c9b022
  //   12c00001 8000c50 4020 1084027 84400 3508ffff 82021 20020022 c 2010ffff 20110000 ae300000 22100001
  //   22310004 ae300000 22100001 22310004 ae300000 22100001 22310004 ae300000 22100001 22310004 ae300000
  //   22100001 22310004 ae300000 22100001 22310004 ae300000 22100001 22310004 ae300000 22100001 22310004
  //   ae300000 22100001 22310004 ae300000 22100001 22310004 ae300000 22100001 22310004 ae300000 22100001
  //   22310004 ae300000 22100001 22310004 ae300000 22100001 22310004 ae300000 22100001 22310004 ae300000
  //   22100001 22310004 22100001 8020 2011003c 8e130000 8e340000 274402a 11000002 ae330000 ae140000
  //   2231fffc 1611fff8 102020 20020022 c 22100004 2011003c 1611fff2 2002000a c 20100000 22100001 102020
  //   20020022 c 22100002 102020 20020022 c 22100003 102020 20020022 c 22100004 102020 20020022 c 22100005
  //   102020 20020022 c 22100006 102020 20020022 c 22100007 102020 20020022 c 22100008 102020 20020022
  //   20020022 c 3e00008
endmodule
