// Logisim project regfile.circ as structural Verilog: 4 circuits, main circuit main
module main (
  input  [4:0] Reg1_num,
  input  [4:0] Reg2,
  input  [4:0] Write_Reg_num,
  input  [31:0] Din,
  input  Write_Enable,
  input  Clock,
  output [31:0] Reg1,
  output [31:0] s0_Value,
  output [31:0] s1_Value,
  output [31:0] s2_Value,
  output [31:0] ra_Value,
  output [31:0] Reg2_2
);

  wire [7:0] decoder_1_out0, decoder_1_out8, decoder_1_out16, decoder_1_out24;
  wire [31:0] r0_q, r1_q, r2_q, r3_q, r4_q, r5_q, r6_q, r7_q, r8_q, r9_q, r10_q, r11_q, r12_q, r13_q, r14_q,
       r15_q, r19_q, r20_q, r21_q, r22_q, r23_q, r24_q, r25_q, r26_q, r27_q, r28_q, r29_q, r30_q;

  Decoder #(.select(5), .disabled(0)) decoder_1 (
    .out0(decoder_1_out0[0]), .out1(decoder_1_out0[1]), .out2(decoder_1_out0[2]), .out3(decoder_1_out0[3]),
    .out4(decoder_1_out0[4]), .out5(decoder_1_out0[5]), .out6(decoder_1_out0[6]), .out7(decoder_1_out0[7]),
    .out8(decoder_1_out8[0]), .out9(decoder_1_out8[1]), .out10(decoder_1_out8[2]), .out11(decoder_1_out8[3]),
    .out12(decoder_1_out8[4]), .out13(decoder_1_out8[5]), .out14(decoder_1_out8[6]),
    .out15(decoder_1_out8[7]), .out16(decoder_1_out16[0]), .out17(decoder_1_out16[1]),
    .out18(decoder_1_out16[2]), .out19(decoder_1_out16[3]), .out20(decoder_1_out16[4]),
    .out21(decoder_1_out16[5]), .out22(decoder_1_out16[6]), .out23(decoder_1_out16[7]),
    .out24(decoder_1_out24[0]), .out25(decoder_1_out24[1]), .out26(decoder_1_out24[2]),
    .out27(decoder_1_out24[3]), .out28(decoder_1_out24[4]), .out29(decoder_1_out24[5]),
    .out30(decoder_1_out24[6]), .out31(decoder_1_out24[7]), .sel(Write_Reg_num), .en(Write_Enable));
  Register #(.width(32)) r1 (.D(Din), .en(decoder_1_out0[1]), .Q(r1_q), .clk(Clock), .clr(1'b0));
  Register #(.width(32)) r0 (.D(Din), .en(decoder_1_out0[0]), .Q(r0_q), .clk(Clock), .clr(1'b1));
  Register #(.width(32)) r8 (.D(Din), .en(decoder_1_out8[0]), .Q(r8_q), .clk(Clock), .clr(1'b0));
  Register #(.width(32)) r9 (.D(Din), .en(decoder_1_out8[1]), .Q(r9_q), .clk(Clock), .clr(1'b0));
  Register #(.width(32)) r16 (.D(Din), .en(decoder_1_out16[0]), .Q(s0_Value), .clk(Clock), .clr(1'b0));
  Register #(.width(32)) r17 (.D(Din), .en(decoder_1_out16[1]), .Q(s1_Value), .clk(Clock), .clr(1'b0));
  Register #(.width(32)) r25 (.D(Din), .en(decoder_1_out24[1]), .Q(r25_q), .clk(Clock), .clr(1'b0));
  Register #(.width(32)) r24 (.D(Din), .en(decoder_1_out24[0]), .Q(r24_q), .clk(Clock), .clr(1'b0));
  Register #(.width(32)) r2 (.D(Din), .en(decoder_1_out0[2]), .Q(r2_q), .clk(Clock), .clr(1'b0));
  Register #(.width(32)) r10 (.D(Din), .en(decoder_1_out8[2]), .Q(r10_q), .clk(Clock), .clr(1'b0));
  Register #(.width(32)) r18 (.D(Din), .en(decoder_1_out16[2]), .Q(s2_Value), .clk(Clock), .clr(1'b0));
  Register #(.width(32)) r26 (.D(Din), .en(decoder_1_out24[2]), .Q(r26_q), .clk(Clock), .clr(1'b0));
  Register #(.width(32)) r3 (.D(Din), .en(decoder_1_out0[3]), .Q(r3_q), .clk(Clock), .clr(1'b0));
  Register #(.width(32)) r11 (.D(Din), .en(decoder_1_out8[3]), .Q(r11_q), .clk(Clock), .clr(1'b0));
  Register #(.width(32)) r19 (.D(Din), .en(decoder_1_out16[3]), .Q(r19_q), .clk(Clock), .clr(1'b0));
  Register #(.width(32)) r27 (.D(Din), .en(decoder_1_out24[3]), .Q(r27_q), .clk(Clock), .clr(1'b0));
  Register #(.width(32)) r4 (.D(Din), .en(decoder_1_out0[4]), .Q(r4_q), .clk(Clock), .clr(1'b0));
  Register #(.width(32)) r12 (.D(Din), .en(decoder_1_out8[4]), .Q(r12_q), .clk(Clock), .clr(1'b0));
  Register #(.width(32)) r20 (.D(Din), .en(decoder_1_out16[4]), .Q(r20_q), .clk(Clock), .clr(1'b0));
  Register #(.width(32)) r28 (.D(Din), .en(decoder_1_out24[4]), .Q(r28_q), .clk(Clock), .clr(1'b0));
  Register #(.width(32)) r5 (.D(Din), .en(decoder_1_out0[5]), .Q(r5_q), .clk(Clock), .clr(1'b0));
  Register #(.width(32)) r13 (.D(Din), .en(decoder_1_out8[5]), .Q(r13_q), .clk(Clock), .clr(1'b0));
  Register #(.width(32)) r21 (.D(Din), .en(decoder_1_out16[5]), .Q(r21_q), .clk(Clock), .clr(1'b0));
  Register #(.width(32)) r29 (.D(Din), .en(decoder_1_out24[5]), .Q(r29_q), .clk(Clock), .clr(1'b0));
  Register #(.width(32)) r6 (.D(Din), .en(decoder_1_out0[6]), .Q(r6_q), .clk(Clock), .clr(1'b0));
  Register #(.width(32)) r14 (.D(Din), .en(decoder_1_out8[6]), .Q(r14_q), .clk(Clock), .clr(1'b0));
  Register #(.width(32)) r22 (.D(Din), .en(decoder_1_out16[6]), .Q(r22_q), .clk(Clock), .clr(1'b0));
  Register #(.width(32)) r30 (.D(Din), .en(decoder_1_out24[6]), .Q(r30_q), .clk(Clock), .clr(1'b0));
  Register #(.width(32)) r7 (.D(Din), .en(decoder_1_out0[7]), .Q(r7_q), .clk(Clock), .clr(1'b0));
  Register #(.width(32)) r15 (.D(Din), .en(decoder_1_out8[7]), .Q(r15_q), .clk(Clock), .clr(1'b0));
  Register #(.width(32)) r23 (.D(Din), .en(decoder_1_out16[7]), .Q(r23_q), .clk(Clock), .clr(1'b0));
  Register #(.width(32)) r31 (.D(Din), .en(decoder_1_out24[7]), .Q(ra_Value), .clk(Clock), .clr(1'b0));
  Multiplexer #(.select(5), .width(32), .enable("false")) multiplexer_1 (
    .in0(r0_q), .in1(r1_q), .in2(r2_q), .in3(r3_q), .in4(r4_q), .in5(r5_q), .in6(r6_q), .in7(r7_q),
    .in8(r8_q), .in9(r9_q), .in10(r10_q), .in11(r11_q), .in12(r12_q), .in13(r13_q), .in14(r14_q),
    .in15(r15_q), .in16(s0_Value), .in17(s1_Value), .in18(s2_Value), .in19(r19_q), .in20(r20_q),
    .in21(r21_q), .in22(r22_q), .in23(r23_q), .in24(r24_q), .in25(r25_q), .in26(r26_q), .in27(r27_q),
    .in28(r28_q), .in29(r29_q), .in30(r30_q), .in31(ra_Value), .out(Reg1), .sel(Reg1_num));
  Multiplexer #(.select(5), .width(32), .enable("false")) multiplexer_2 (
    .in0(r0_q), .in1(r1_q), .in2(r2_q), .in3(r3_q), .in4(r4_q), .in5(r5_q), .in6(r6_q), .in7(r7_q),
    .in8(r8_q), .in9(r9_q), .in10(r10_q), .in11(r11_q), .in12(r12_q), .in13(r13_q), .in14(r14_q),
    .in15(r15_q), .in16(s0_Value), .in17(s1_Value), .in18(s2_Value), .in19(r19_q), .in20(r20_q),
    .in21(r21_q), .in22(r22_q), .in23(r23_q), .in24(r24_q), .in25(r25_q), .in26(r26_q), .in27(r27_q),
    .in28(r28_q), .in29(r29_q), .in30(r30_q), .in31(ra_Value), .out(Reg2_2), .sel(Reg2));

  // Other names for the same wires on the sheet: clk = Clock; ra[31:0] = ra_Value; reg2_num[4:0] = Reg2;
  //   reg2_t[31:0] = Reg2_2; s0[31:0] = s0_Value; s1[31:0] = s1_Value; s2[31:0] = s2_Value; WE = Write_Enable;
  //   write_data[31:0] = Din

  // Notes on the sheet:
  //   输入引脚
  //   输出引脚
  //   Debug引脚，便于观测寄存器值
  //   请勿修改引脚以及封装，直接使用隧道连接电路
endmodule

module test (
);

  wire undriven;

  main main_1 (.Clock(undriven));  // open: Reg1_num, Reg2, Write_Reg_num, Din, Write_Enable, Reg1, Reg2_2, s0_Value, s1_Value, s2_Value, ra_Value
endmodule

module MIPSRegisters (
  input  [4:0] Reg1_num,
  input  [4:0] Reg2,
  input  [4:0] Write_Reg_num,
  input  [31:0] Din,
  input  Write_Enable,
  input  Clock,
  output [31:0] Reg1,
  output [31:0] s0_Value,
  output [31:0] s1_Value,
  output [31:0] s2_Value,
  output [31:0] ra_Value,
  output [31:0] Reg2_2
);

  wire [31:0] decoder_1_out0, multiplexer_1_out, r0_q, r1_q, r2_q, r3_q, r4_q, r5_q, r6_q, r7_q, r8_q, r9_q,
       r10_q, r11_q, r12_q, r13_q, r14_q, r15_q, r19_q, r20_q, r21_q, r22_q, r23_q, r24_q, r25_q, r26_q,
       r27_q, r28_q, r29_q, r30_q;

  Decoder #(.select(5), .enable("false")) decoder_1 (
    .out0(decoder_1_out0[0]), .out1(decoder_1_out0[1]), .out2(decoder_1_out0[2]), .out3(decoder_1_out0[3]),
    .out4(decoder_1_out0[4]), .out5(decoder_1_out0[5]), .out6(decoder_1_out0[6]), .out7(decoder_1_out0[7]),
    .out8(decoder_1_out0[8]), .out9(decoder_1_out0[9]), .out10(decoder_1_out0[10]),
    .out11(decoder_1_out0[11]), .out12(decoder_1_out0[12]), .out13(decoder_1_out0[13]),
    .out14(decoder_1_out0[14]), .out15(decoder_1_out0[15]), .out16(decoder_1_out0[16]),
    .out17(decoder_1_out0[17]), .out18(decoder_1_out0[18]), .out19(decoder_1_out0[19]),
    .out20(decoder_1_out0[20]), .out21(decoder_1_out0[21]), .out22(decoder_1_out0[22]),
    .out23(decoder_1_out0[23]), .out24(decoder_1_out0[24]), .out25(decoder_1_out0[25]),
    .out26(decoder_1_out0[26]), .out27(decoder_1_out0[27]), .out28(decoder_1_out0[28]),
    .out29(decoder_1_out0[29]), .out30(decoder_1_out0[30]), .out31(decoder_1_out0[31]), .sel(Write_Reg_num));
  Multiplexer #(.width(32), .enable("false")) multiplexer_1 (
    .in0({32{1'b0}}), .in1(decoder_1_out0), .out(multiplexer_1_out), .sel(Write_Enable));
  Register #(.width(32)) r0 (.D(Din), .en(multiplexer_1_out[0]), .Q(r0_q), .clk(Clock), .clr(1'b1));
  Register #(.width(32)) r1 (.D(Din), .en(multiplexer_1_out[1]), .Q(r1_q), .clk(Clock), .clr(1'b0));
  Register #(.width(32)) r9 (.D(Din), .en(multiplexer_1_out[9]), .Q(r9_q), .clk(Clock), .clr(1'b0));
  Register #(.width(32)) r8 (.D(Din), .en(multiplexer_1_out[8]), .Q(r8_q), .clk(Clock), .clr(1'b0));
  Register #(.width(32)) r16 (.D(Din), .en(multiplexer_1_out[16]), .Q(s0_Value), .clk(Clock), .clr(1'b0));
  Register #(.width(32)) r17 (.D(Din), .en(multiplexer_1_out[17]), .Q(s1_Value), .clk(Clock), .clr(1'b0));
  Register #(.width(32)) r25 (.D(Din), .en(multiplexer_1_out[25]), .Q(r25_q), .clk(Clock), .clr(1'b0));
  Register #(.width(32)) r24 (.D(Din), .en(multiplexer_1_out[24]), .Q(r24_q), .clk(Clock), .clr(1'b0));
  Register #(.width(32)) r2 (.D(Din), .en(multiplexer_1_out[2]), .Q(r2_q), .clk(Clock), .clr(1'b0));
  Register #(.width(32)) r10 (.D(Din), .en(multiplexer_1_out[10]), .Q(r10_q), .clk(Clock), .clr(1'b0));
  Register #(.width(32)) r18 (.D(Din), .en(multiplexer_1_out[18]), .Q(s2_Value), .clk(Clock), .clr(1'b0));
  Register #(.width(32)) r26 (.D(Din), .en(multiplexer_1_out[26]), .Q(r26_q), .clk(Clock), .clr(1'b0));
  Register #(.width(32)) r3 (.D(Din), .en(multiplexer_1_out[3]), .Q(r3_q), .clk(Clock), .clr(1'b0));
  Register #(.width(32)) r11 (.D(Din), .en(multiplexer_1_out[11]), .Q(r11_q), .clk(Clock), .clr(1'b0));
  Register #(.width(32)) r19 (.D(Din), .en(multiplexer_1_out[19]), .Q(r19_q), .clk(Clock), .clr(1'b0));
  Register #(.width(32)) r27 (.D(Din), .en(multiplexer_1_out[27]), .Q(r27_q), .clk(Clock), .clr(1'b0));
  Register #(.width(32)) r4 (.D(Din), .en(multiplexer_1_out[4]), .Q(r4_q), .clk(Clock), .clr(1'b0));
  Register #(.width(32)) r12 (.D(Din), .en(multiplexer_1_out[12]), .Q(r12_q), .clk(Clock), .clr(1'b0));
  Register #(.width(32)) r20 (.D(Din), .en(multiplexer_1_out[20]), .Q(r20_q), .clk(Clock), .clr(1'b0));
  Register #(.width(32)) r28 (.D(Din), .en(multiplexer_1_out[28]), .Q(r28_q), .clk(Clock), .clr(1'b0));
  Register #(.width(32)) r5 (.D(Din), .en(multiplexer_1_out[5]), .Q(r5_q), .clk(Clock), .clr(1'b0));
  Register #(.width(32)) r13 (.D(Din), .en(multiplexer_1_out[13]), .Q(r13_q), .clk(Clock), .clr(1'b0));
  Register #(.width(32)) r21 (.D(Din), .en(multiplexer_1_out[21]), .Q(r21_q), .clk(Clock), .clr(1'b0));
  Register #(.width(32)) r29 (.D(Din), .en(multiplexer_1_out[29]), .Q(r29_q), .clk(Clock), .clr(1'b0));
  Register #(.width(32)) r6 (.D(Din), .en(multiplexer_1_out[6]), .Q(r6_q), .clk(Clock), .clr(1'b0));
  Register #(.width(32)) r14 (.D(Din), .en(multiplexer_1_out[14]), .Q(r14_q), .clk(Clock), .clr(1'b0));
  Register #(.width(32)) r22 (.D(Din), .en(multiplexer_1_out[22]), .Q(r22_q), .clk(Clock), .clr(1'b0));
  Register #(.width(32)) r30 (.D(Din), .en(multiplexer_1_out[30]), .Q(r30_q), .clk(Clock), .clr(1'b0));
  Register #(.width(32)) r7 (.D(Din), .en(multiplexer_1_out[7]), .Q(r7_q), .clk(Clock), .clr(1'b0));
  Register #(.width(32)) r15 (.D(Din), .en(multiplexer_1_out[15]), .Q(r15_q), .clk(Clock), .clr(1'b0));
  Register #(.width(32)) r23 (.D(Din), .en(multiplexer_1_out[23]), .Q(r23_q), .clk(Clock), .clr(1'b0));
  Register #(.width(32)) r31 (.D(Din), .en(multiplexer_1_out[31]), .Q(ra_Value), .clk(Clock), .clr(1'b0));
  Multiplexer #(.select(5), .width(32), .enable("false")) multiplexer_2 (
    .in0(r0_q), .in1(r1_q), .in2(r2_q), .in3(r3_q), .in4(r4_q), .in5(r5_q), .in6(r6_q), .in7(r7_q),
    .in8(r8_q), .in9(r9_q), .in10(r10_q), .in11(r11_q), .in12(r12_q), .in13(r13_q), .in14(r14_q),
    .in15(r15_q), .in16(s0_Value), .in17(s1_Value), .in18(s2_Value), .in19(r19_q), .in20(r20_q),
    .in21(r21_q), .in22(r22_q), .in23(r23_q), .in24(r24_q), .in25(r25_q), .in26(r26_q), .in27(r27_q),
    .in28(r28_q), .in29(r29_q), .in30(r30_q), .in31(ra_Value), .out(Reg1), .sel(Reg1_num));
  Multiplexer #(.select(5), .width(32), .enable("false")) multiplexer_3 (
    .in0(r0_q), .in1(r1_q), .in2(r2_q), .in3(r3_q), .in4(r4_q), .in5(r5_q), .in6(r6_q), .in7(r7_q),
    .in8(r8_q), .in9(r9_q), .in10(r10_q), .in11(r11_q), .in12(r12_q), .in13(r13_q), .in14(r14_q),
    .in15(r15_q), .in16(s0_Value), .in17(s1_Value), .in18(s2_Value), .in19(r19_q), .in20(r20_q),
    .in21(r21_q), .in22(r22_q), .in23(r23_q), .in24(r24_q), .in25(r25_q), .in26(r26_q), .in27(r27_q),
    .in28(r28_q), .in29(r29_q), .in30(r30_q), .in31(ra_Value), .out(Reg2_2), .sel(Reg2));

  // Other names for the same wires on the sheet: clk = Clock; ra[31:0] = ra_Value; reg2_num[4:0] = Reg2;
  //   reg2_t[31:0] = Reg2_2; s0[31:0] = s0_Value; s1[31:0] = s1_Value; s2[31:0] = s2_Value; WE = Write_Enable;
  //   write_data[31:0] = Din

  // Notes on the sheet:
  //   输入引脚
  //   输出引脚
  //   Debug引脚，便于观测寄存器值
  //   请勿修改引脚以及封装，直接使用隧道连接电路
endmodule

// Result
module SumCircuit (
  input  in_1
);

  wire Clk, or_1_out;
  wire [0:0] counter_2_carry;
  wire [4:0] Circ;
  wire [5:5] not_1_out;
  wire [31:0] multiplexer_1_out, Num1, Num2, ram_1_data, Result;

  Clock clock_1 (.out(Clk));
  // Probe on Circ
  Counter #(.width(5), .max('h1f)) counter_1 (
    .count(1'b1), .Q(Circ), .clk(counter_2_carry[0]), .clr(in_1));  // open: load, D, carry
  Counter #(.width(1), .max('h1)) counter_2 (
    .load(1'b1), .count(1'b1), .carry(counter_2_carry[0]), .clk(Clk));  // open: D, Q, clr
  // Probe on Num1
  RAM #(.addrWidth(6), .dataWidth(32), .bus("separate")) ram_1 (
    .addr({not_1_out[5], Circ}), .din(Result), .data(ram_1_data), .str(1'b1), .sel(1'b1),
    .clk(counter_2_carry[0]), .ld(1'b1), .clr(in_1));
  Multiplexer #(.width(32), .enable("false")) multiplexer_1 (
    .in0(Result), .in1(ram_1_data), .out(multiplexer_1_out), .sel(counter_2_carry[0]));
  not not_1 (not_1_out[5], counter_2_carry[0]);
  Hex_Digit_Display hex_digit_display_1 (.value(Result[27:24]), .dp(1'b0));
  Hex_Digit_Display hex_digit_display_2 (.value(Result[31:28]), .dp(1'b0));
  // Probe on Num2
  Hex_Digit_Display hex_digit_display_3 (.value(Result[23:20]), .dp(1'b0));
  Hex_Digit_Display hex_digit_display_4 (.value(Result[19:16]), .dp(1'b0));
  main main_1 (
    .Reg1_num(5'b00001), .Reg2(5'b00010), .Write_Reg_num({3'b000, not_1_out[5], counter_2_carry[0]}),
    .Din(multiplexer_1_out), .Write_Enable(or_1_out), .Clock(Clk), .Reg1(Num1), .Reg2_2(Num2));  // open: s0_Value, s1_Value, s2_Value, ra_Value
  Hex_Digit_Display hex_digit_display_5 (.value(Result[11:8]), .dp(1'b0));
  Hex_Digit_Display hex_digit_display_6 (.value(Result[15:12]), .dp(1'b0));
  or or_1 (or_1_out, ~Circ[0], ~Circ[1], ~Circ[2], ~Circ[3], ~Circ[4], counter_2_carry[0]);  // OR_Gate
  Hex_Digit_Display hex_digit_display_7 (.value(Result[3:0]), .dp(1'b0));
  Hex_Digit_Display hex_digit_display_8 (.value(Result[7:4]), .dp(1'b0));
  // Probe on Result
  ALU alu_1 (
    .AluOP(4'b0101), .X(Num1), .Result(Result), .Y(Num2));  // open: Equal, Signed_Overflow, Result_2, UnSigned_Overflow

  // Other names for the same wires on the sheet: Clr = in_1

  // Notes on the sheet:
  //   时钟信号
  //   清零信号(RAM载入数据前先清零)
  //   输入引脚
  //   输出引脚
  //   探测区域
endmodule
